# Fritzing sketch Temp Box1 (saved by Fritzing 0.9.3b)
breadboards: 2

parts:
  Part1 = Arduino Uno (Rev3)
  U1 = AD5206 Digital Potentiometer [maximum_resistance=10kΩ package="DIP28 [THT]"]
  DS1 = DS1809 [part_number=DS1809 package=DS1806]  # not connected
  U3 = MCP42xxx [package=so014]  # not connected
  U4 = MCP41xxx [package=so08]  # not connected

nets:
  N1: Part1.D10_PWM/SS, U1.CS
  N2: Part1.D11_PWM/MOSI, U1.SDI
  N3: Part1.D13/SCK, U1.CLK
  GND: Part1.GND, U1.Gnd, U1.Vss
  5V: Part1.5V, U1.A6, U1.Vdd, U1.A5

// code stored in the sketch: Untitled7.ino
#include <SPI.h>

set pin 10 as the slave select for the digital pot:
const int slaveSelectPin = 10;

void setup() {

  pinMode(slaveSelectPin, OUTPUT);

  SPI.begin();
}

void loop() {

  for (int channel = 0; channel < 6; channel++) {

    for (int level = 0; level < 255; level++) {
      digitalPotWrite(channel, level);
      delay(10);
    }

    delay(100);

    for (int level = 0; level < 255; level++) {
      digitalPotWrite(channel, 255 - level);
      delay(10);
    }
  }

}

void digitalPotWrite(int address, int value) {

  digitalWrite(slaveSelectPin, LOW);

  SPI.transfer(address);
  SPI.transfer(value);

  digitalWrite(slaveSelectPin, HIGH);
}
